# Fritzing sketch CABR (saved by Fritzing 0.9.3b)
breadboards: 1

parts:
  Q1 = NPN-Transistor [package="TO92 [THT]"]
  U2 = Voltage Regulator - 5V [part_number="This goes on backward to save space" package="TO220 [THT]"]
  C1 = Electrolytic Capacitor [capacitance=10µF voltage=20V package="100 mil [THT, electrolytic]"]
  C2 = Electrolytic Capacitor [capacitance=10µF voltage=20V package="100 mil [THT, electrolytic]"]
  Q2 = MOSFET-NCHANNEL [package=to220v]
  U1 = attiny85 [package=dip]
  J1 = Screw terminal - 2 pins [part_number=Power package=THT]
  J2 = screw terminal, 3 pins
  R1 = Resistor [tolerance=±5% resistance=10k package="0805 [SMD]"]
  R3 = Vertical Resistor [tolerance=±5% resistance=10k package=THT]
  J3 = Screw terminal - 2 pins [part_number=Power package=THT]
  J4 = Screw terminal - 2 pins [package=THT]
  R4 = Vertical Resistor [tolerance=±5% resistance=10k package=THT]

nets:
  N1: Q1.E, Q2.D
  N2: Q1.B, U2.output_voltage, Q2.G
  N3: Q1.C, U1.Pin_3
  N4: U2.input_voltage, C2.+
  N5: U2.GND, C1.-, C2.-, U1.Pin_4, J1.pin2, R1.Pin_1, R3.Pin_0, J3.pin1, R4.Pin_0
  N6: C1.+, J1.pin1
  N7: Q2.S, J3.pin2
  N8: U1.Pin_6, J2.pin1, R3.Pin_1
  N9: U1.Pin_7, J2.pin3, R1.Pin_0
  N10: U1.Pin_8, J2.pin2, J4.pin1
  N11: J4.pin2, R4.Pin_1

custom parts:
  Vertical Resistor: A generic resistor (0.25W)
